# Fritzing sketch estacion de monitoreo (saved by Fritzing 0.9.3b)
breadboards: 1

parts:
  ESP_WROOM_32 = ESP32-38PinWide [part_number=ESP32-38PinWide]
  Sensor_de_Lluvia_YL-83 = YL-83 Rain Sensor - Detection Board
  YL-83_-_Control_Board1 = YL-83 Rain Sensor - Control Board
  Sensor_de_Sonido = KY-038 Sound Sensor Module
  BME280_-_Environmental_Sensor = Adafruit BME280 [part_number="Adafruit #2652"]
  MQ-135 = MQ135 Hava Kalite Sensörü
  RASPBERRY_PI_3 = Raspberry Pi 3 [part_number=RPI-3-V1.2]  # not connected
  PANTALLA_7''_RASPBERRY_PI_3 = Adafruit 3.5in 480x320 TFT FeatherWing [part_number="Adafrruit #3651"]  # not connected

nets:
  N1: ESP_WROOM_32.GPIO39, YL-83_-_Control_Board1.AO
  N2: ESP_WROOM_32.GPIO34, YL-83_-_Control_Board1.DO
  N3: ESP_WROOM_32.GPIO14, Sensor_de_Sonido.AO
  GND: ESP_WROOM_32.GND, ESP_WROOM_32.GPIO6, ESP_WROOM_32.GPIO7, ESP_WROOM_32.GPIO15, ESP_WROOM_32.GPIO0, ESP_WROOM_32.GPIO4, ESP_WROOM_32.GPIO17, ESP_WROOM_32.GPIO5, ESP_WROOM_32.GPIO18, ESP_WROOM_32.GPIO21, ESP_WROOM_32.GPIO3, ESP_WROOM_32.GPIO22, YL-83_-_Control_Board1.GND, Sensor_de_Sonido.G, BME280_-_Environmental_Sensor.GND, BME280_-_Environmental_Sensor.SDI/SDA, BME280_-_Environmental_Sensor.SCK/SCL, MQ-135.GND
  VCC: ESP_WROOM_32.VIN, YL-83_-_Control_Board1.VCC, Sensor_de_Sonido.VCC, BME280_-_Environmental_Sensor.VCC
  N4: Sensor_de_Lluvia_YL-83.POS, YL-83_-_Control_Board1.POS
  N5: Sensor_de_Lluvia_YL-83.NEG, YL-83_-_Control_Board1.NEG

custom parts:
  ESP32-38PinWide: Generic 38-Pin ESP32 with wide format (only access to one side of pins on a breadboard) based on Stephen Lilley's HiLetgo ESP-WROOM-32 ESP32 ESP-32S Development Board.
  YL-83 Rain Sensor - Detection Board: The YL-83 is a rain sensor that has more resistance when dry and less resistance when wet. The module runs at 5V.
  YL-83 Rain Sensor - Control Board: The YL-83 is a rain sensor that has more resistance when dry and less resistance when wet. The module runs at 5V.
  Adafruit BME280: Bosch has stepped up their game with their new BME280 sensor, an environmental sensor with temperature, barometric pressure and humidity! This sensor is great for all sorts of indoor environmental sensing and can even be used in both I2C and SPI! This precision sensor from Bosch is the best low-cost sensing solution for measuring humidity with ±3% accuracy, barometric pressure with ±1 hPa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
  Adafruit 3.5in 480x320 TFT FeatherWing: Spice up your Feather project with a beautiful 3.5" touchscreen display shield with built in microSD card socket. This TFT display is 3.5" diagonal with a bright 6 white-LED backlight. You get a massive 480x320 pixels with individual 16-bit color pixel control. It has way more resolution than a black and white 128x64 display, and twice as much as our 2.4" TFT FeatherWing. As a bonus, this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
